# Fritzing sketch LedPcb (saved by Fritzing 0.9.3b)
circuit board: 6.46325cm x 4.43913cm
breadboards: 1

parts:
  J7 = female pin header, 3 pins [form="♀ (female)"]
  J8 = shrouded pin header, 10 pins [form="♂ (shrouded male)"]
  J6 = female pin header, 3 pins [form="♀ (female)"]

nets:
  N1: J7.pin1, J8.pin9
  N2: J7.pin2, J8.pin10
  N3: J7.pin3, J8.pin8
  N4: J8.pin3, J6.pin1
  N5: J8.pin4, J6.pin2
  N6: J8.pin5, J6.pin3

notes:
  G
  R
  +
  -
  B
